// Logisim project log.circ as structural Verilog: 4 circuits, main circuit main
module main (
  input  [3:0] in_1,
  output [3:0] out_2
);

  wire clock_1_out, decoder_1_out0, decoder_1_out1, decoder_1_out2, decoder_1_out3, not_1_out, or_1_out;
  wire [1:0] t_ff_1_q;
  wire [3:0] counter_1_q;
  wire [7:0] alu_1_out_5, controlled_buffer_1_out, regdec_1_e_2, regdec_1_e_2_2, register_1_q, register_2_q,
       register_3_q, register_4_q, register_5_q, register_6_q, register_7_q, register_8_q, register_9_q,
       register_10_q, register_12_q, register_13_q;
  wire [15:0] controlled_buffer_9_out, controlled_buffer_10_out, controlled_buffer_11_out, counter_2_q,
       register_11_q, shreg_1_out_3;
  wire [31:0] rom_1_data;

  Register register_1 (.Q(register_1_q), .clk(regdec_1_e_2_2[7]));  // open: D, en, clr
  assign controlled_buffer_1_out = regdec_1_e_2_2[6] ? register_1_q : 8'bz;  // Controlled_Buffer controlled_buffer_1
  Register register_2 (.D(controlled_buffer_1_out), .Q(register_2_q), .clk(regdec_1_e_2_2[5]));  // open: en, clr
  assign controlled_buffer_1_out = regdec_1_e_2_2[4] ? register_2_q : 8'bz;  // Controlled_Buffer controlled_buffer_2
  assign controlled_buffer_1_out = regdec_1_e_2_2[2] ? register_4_q : 8'bz;  // Controlled_Buffer controlled_buffer_3
  Register register_3 (.D(controlled_buffer_1_out), .Q(register_3_q), .clk(regdec_1_e_2_2[1]));  // open: en, clr
  Register register_4 (.D(controlled_buffer_1_out), .Q(register_4_q), .clk(regdec_1_e_2_2[3]));  // open: en, clr
  Register register_5 (.D(controlled_buffer_1_out), .Q(register_5_q), .clk(regdec_1_e_2[7]));  // open: en, clr
  assign controlled_buffer_1_out = regdec_1_e_2_2[0] ? register_3_q : 8'bz;  // Controlled_Buffer controlled_buffer_4
  T_Flip_Flop t_ff_1 (.clk(not_1_out), .T(not_1_out), .Q(t_ff_1_q[0]));  // open: Qn, preset, reset, en
  not not_1 (not_1_out, clock_1_out);
  T_Flip_Flop t_ff_2 (.clk(clock_1_out), .T(clock_1_out), .Q(t_ff_1_q[1]));  // open: Qn, preset, reset, en
  Clock clock_1 (.out(clock_1_out));
  Register register_6 (.D(controlled_buffer_1_out), .Q(register_6_q), .clk(regdec_1_e_2[5]));  // open: en, clr
  assign controlled_buffer_1_out = regdec_1_e_2[6] ? register_5_q : 8'bz;  // Controlled_Buffer controlled_buffer_5
  Register register_7 (
    .D(controlled_buffer_1_out), .Q(register_7_q), .clk(controlled_buffer_9_out[2]));  // open: en, clr
  Counter #(.width(4), .max('hf)) counter_1 (
    .Q(counter_1_q), .clk(decoder_1_out0));  // open: load, D, count, carry, clr
  Decoder #(.select(2), .disabled(0), .enable("false")) decoder_1 (
    .out0(decoder_1_out0), .out1(decoder_1_out1), .out2(decoder_1_out2), .out3(decoder_1_out3), .sel(t_ff_1_q));
  assign controlled_buffer_1_out = regdec_1_e_2[2] ? register_8_q : 8'bz;  // Controlled_Buffer controlled_buffer_6
  Register register_8 (.D(controlled_buffer_1_out), .Q(register_8_q), .clk(regdec_1_e_2[3]));  // open: en, clr
  assign controlled_buffer_1_out = regdec_1_e_2[4] ? register_6_q : 8'bz;  // Controlled_Buffer controlled_buffer_7
  or or_1 (or_1_out, decoder_1_out1, decoder_1_out2, decoder_1_out3);
  assign controlled_buffer_1_out = regdec_1_e_2[0] ? register_9_q : 8'bz;  // Controlled_Buffer controlled_buffer_8
  Register register_9 (.D(controlled_buffer_1_out), .Q(register_9_q), .clk(regdec_1_e_2[1]));  // open: en, clr
  ROM #(.addrWidth(4), .dataWidth(32)) rom_1 (.addr(in_1), .data(rom_1_data));  // open: sel
  // Probe on shreg_1_out_3
  shreg shreg_1 (.in_1(controlled_buffer_1_out), .in_2(controlled_buffer_9_out[3]), .out_3(shreg_1_out_3));
  // Probe on controlled_buffer_1_out
  regdec regdec_1 (
    .E_2({regdec_1_e_2_2[6], regdec_1_e_2_2[4], regdec_1_e_2_2[2], regdec_1_e_2_2[0], regdec_1_e_2[6], regdec_1_e_2[4], regdec_1_e_2[2], regdec_1_e_2[0]}),
    .E(controlled_buffer_10_out[8]),
    .S_2({regdec_1_e_2_2[7], regdec_1_e_2_2[5], regdec_1_e_2_2[3], regdec_1_e_2_2[1], regdec_1_e_2[7], regdec_1_e_2[5], regdec_1_e_2[3], regdec_1_e_2[1]}),
    .S(controlled_buffer_9_out[8]), .in_2(register_10_q));
  Register register_10 (
    .D(controlled_buffer_1_out), .Q(register_10_q), .clk(controlled_buffer_9_out[1]));  // open: en, clr
  assign controlled_buffer_9_out = or_1_out ? rom_1_data[15:0] : 16'bz;  // Controlled_Buffer controlled_buffer_9
  Pull_Resistor pull_resistor_1 (.node(controlled_buffer_9_out));
  assign controlled_buffer_10_out = decoder_1_out3 ? rom_1_data[31:16] : 16'bz;  // Controlled_Buffer controlled_buffer_10
  Pull_Resistor pull_resistor_2 (.node(controlled_buffer_10_out));
  assign controlled_buffer_11_out = controlled_buffer_10_out[3] ? counter_2_q : 16'bz;  // Controlled_Buffer controlled_buffer_11
  Counter #(.width(16), .max('hffff)) counter_2 (
    .load(controlled_buffer_10_out[2]), .D(shreg_1_out_3), .count(controlled_buffer_10_out[1]),
    .Q(counter_2_q), .clk(controlled_buffer_9_out[4]));  // open: carry, clr
  // Probe on controlled_buffer_1_out
  Register #(.width(16)) register_11 (
    .D(controlled_buffer_11_out), .Q(register_11_q), .clk(controlled_buffer_9_out[5]));  // open: en, clr
  RAM #(.addrWidth(16)) ram_1 (
    .addr(register_11_q), .data(controlled_buffer_1_out), .clk(controlled_buffer_9_out[6]),
    .ld(controlled_buffer_10_out[4]));  // open: sel, clr
  ALU alu_1 (
    .A(controlled_buffer_1_out), .B(register_12_q), .in_3(controlled_buffer_10_out[5]), .out_6(out_2),
    .in_4(controlled_buffer_10_out[7:6]), .out_5(alu_1_out_5));
  Register register_12 (
    .D(controlled_buffer_1_out), .Q(register_12_q), .clk(controlled_buffer_9_out[7]));  // open: en, clr
  Register register_13 (.D(alu_1_out_5), .Q(register_13_q), .clk(controlled_buffer_9_out[0]));  // open: en, clr
  assign controlled_buffer_1_out = controlled_buffer_10_out[0] ? register_13_q : 8'bz;  // Controlled_Buffer controlled_buffer_12

  // Notes on the sheet:
  //   e
  //   s
  //   E
  //   S
endmodule

module shreg (
  input  [7:0] in_1,
  input  in_2,
  output [15:0] out_3
);

  Register register_1 (.D(in_1), .Q(out_3[7:0]), .clk(in_2));  // open: en, clr
  Register register_2 (.D(out_3[7:0]), .Q(out_3[15:8]), .clk(in_2));  // open: en, clr
endmodule

module regdec (
  input  E,
  input  [7:0] in_2,
  input  S,
  output [7:0] E_2,
  output [7:0] S_2
);

  Decoder #(.select(3), .disabled(0)) decoder_1 (
    .out0(E_2[0]), .out1(E_2[1]), .out2(E_2[2]), .out3(E_2[3]), .out4(E_2[4]), .out5(E_2[5]), .out6(E_2[6]),
    .out7(E_2[7]), .sel(in_2[2:0]), .en(E));
  Decoder #(.select(3), .disabled(0)) decoder_2 (
    .out0(S_2[0]), .out1(S_2[1]), .out2(S_2[2]), .out3(S_2[3]), .out4(S_2[4]), .out5(S_2[5]), .out6(S_2[6]),
    .out7(S_2[7]), .sel(in_2[5:3]), .en(S));
endmodule

module ALU (
  input  [7:0] A,
  input  [7:0] B,
  input  in_3,
  input  [1:0] in_4,
  output [7:0] out_5,
  output [3:0] out_6
);

  wire [7:0] adder_1_out, and_1_out, not_1_out;

  Pull_Resistor pull_resistor_1 (.node(A));
  Pull_Resistor pull_resistor_2 (.node(B));
  Adder adder_1 (.a(A), .b(B), .out(adder_1_out), .cin(in_3), .cout(out_6[3]));
  assign and_1_out = A & B;  // AND_Gate and_1, 8 bits wide
  assign not_1_out = ~A;  // NOT_Gate not_1, 8 bits wide
  Comparator comparator_1 (.a(A), .b(B), .gt(out_6[2]), .eq(out_6[1]));  // open: lt
  or or_1 (out_6[0], A[0], A[1], A[2], A[3], A[4], A[5], A[6], A[7]);
  Pull_Resistor pull_resistor_3 (.node(out_6));
  Multiplexer #(.select(2), .width(8), .disabled(0), .enable("false")) multiplexer_1 (
    .in0(adder_1_out), .in1(and_1_out), .in2(not_1_out), .out(out_5), .sel(in_4));  // open: in3
endmodule
